# Fritzing sketch Air Quality Sensor (saved by Fritzing 0.9.9b)
breadboards: 1

parts:
  Part1 = Adafruit SHT31-D [part_number="Adafruit #2857"]
  U1 = Mini-360 DC-DC Buck converter [package=THT]
  M1 = LILYGO TTGO-T SIM7000G
  JP2 = Header 5 [package=1x05-1mm]
  JP3 = Header 6 [package=1x06-smd-female-v2]
  R1 = Resistor [tolerance=±5% resistance=10k package="2512 [SMD]"]
  JP4 = Header 6 [package=1x06-smd-female-v2]
  R2 = Resistor [tolerance=±5% resistance=10k package="2512 [SMD]"]
  R3 = Resistor [tolerance=±5% resistance=10k package="2512 [SMD]"]
  Q1 = NPN-Transistor [package="TO92 [THT]"]
  Q2 = NPN-Transistor [package="TO92 [THT]"]
  Q3 = NPN-Transistor [package="TO92 [THT]"]

nets:
  N1: Part1.SDA, M1.pin_27, JP2.4, R2.Pin_1
  N2: Part1.VCC, U1.IN+, M1.pin_1, M1.pin_30, R1.Pin_0, R2.Pin_0, R3.Pin_0
  N3: Part1.GND, U1.IN-, Q1.C, Q2.C, Q3.C
  N4: Part1.SCL, M1.pin_28, JP2.3, R3.Pin_1
  N5: U1.OUT+, JP2.5, JP3.6, JP4.5, JP4.6
  N6: U1.OUT-, JP2.1, JP2.2, JP3.5, Q1.E, Q2.E, Q3.E
  N7: M1.pin_3, JP3.3
  N8: M1.pin_4, JP3.2
  N9: M1.pin_5, JP4.3
  N10: M1.pin_6, JP4.2
  N11: M1.pin_14, Q1.B, Q2.B, Q3.B
  N12: JP3.1, JP3.4, R1.Pin_1, JP4.1, JP4.4

custom parts:
  Adafruit SHT31-D: Sensirion Temperature/Humidity sensors are some of the finest & highest-accuracy devices you can get. And, finally we have some that have a true I2C interface for easy reading. The SHT31-D sensor has an excellent ±2% relative humidity and ±0.3°C accuracy for most uses. We now use the version with a PTFE filter, it'll stay clean while still allowing humidity measurements to work Unlike earlier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
  Mini-360 DC-DC Buck converter: Mini-360 DC-DC Buck converter. Tiny buck step down voltage converter, input voltage 4.75 to 23V output 1 to 17V adjustable. Available from ebay and the like.
  LILYGO TTGO-T SIM7000G: LILYGO® TTGO T-SIM7000G Module ESP32-WROVER-B Chip WiFi Bluetooth 18560 Battery Holder Solar Charge Development Board.
