# Fritzing sketch Air Quality Sensor Wiring Fritzing (saved by Fritzing 0.9.9b)
breadboards: 1

parts:
  Part1 = Adafruit SHT31-D [part_number="Adafruit #2857"]
  U1 = Mini-360 DC-DC Buck converter [package=THT]
  M1 = LILYGO TTGO-T SIM7000G
  JP2 = Header 5 [package=1x05-1mm]
  JP3 = Header 6 [package=1x06-smd-female-v2]
  R1 = Resistor [tolerance=±5% resistance=10k package="2512 [SMD]"]
  JP4 = Header 6 [package=1x06-smd-female-v2]
  R2 = Resistor [tolerance=±5% resistance=10k package="2512 [SMD]"]
  R3 = Resistor [tolerance=±5% resistance=10k package="2512 [SMD]"]
  R4 = Resistor [tolerance=±5% resistance=1k package="0603 [SMD]"]
  FET1 = STP16NF06 N-Channel Power MOSFET
  R6 = Resistor [tolerance=±5% resistance=100k package="0603 [SMD]"]
  C4 = Electrolytic Capacitor [capacitance=100µF voltage=10V package="200 mil [THT, electrolytic]"]
  C5 = Electrolytic Capacitor [capacitance=100µF voltage=10V package="200 mil [THT, electrolytic]"]
  J4 = Camdenboss CTB0158-7 [part_number=CTB0158-7 package=THT]
  U4 = Hirose DF13 Series Header [part_number=DF13#-2P-1.25V package=DF13C-2P-1.25V]
  U5 = Hirose DF13 Series Header [part_number=DF13#-2P-1.25V package=DF13C-2P-1.25V]
  U6 = Hirose DF13 Series Header [part_number=DF13#-2P-1.25V package=DF13C-2P-1.25V]
  Part2 = Solar Cell
  C6 = Electrolytic Capacitor [capacitance=100µF voltage=10V package="200 mil [THT, electrolytic]"]

nets:
  N1: Part1.SDA, M1.pin_27, JP2.4, R2.Pin_1
  N2: Part1.VCC, U1.IN+, M1.pin_1, M1.pin_30, R1.Pin_0, R2.Pin_0, R3.Pin_0, C5.+, J4.pin1
  N3: Part1.GND, U1.OUT-, JP2.1, JP2.2, JP3.5, JP4.5, C4.-, J4.pin3
  N4: Part1.SCL, M1.pin_28, JP2.3, R3.Pin_1
  N5: U1.IN-, FET1.drain
  N6: U1.OUT+, JP2.5, JP3.6, JP4.6, C4.+, J4.pin2
  N7: M1.pin_2, M1.pin_18, FET1.source, R6.Pin_0, C5.-
  N8: M1.pin_3, JP3.3
  N9: M1.pin_4, JP3.2
  N10: M1.pin_5, JP4.3
  N11: M1.pin_6, JP4.2
  N12: M1.pin_15, R4.Pin_0
  N13: M1.pin_23, J4.pin4
  N14: M1.pin_24, J4.pin5
  N15: M1.pin_25, J4.pin6
  N16: M1.pin_26, J4.pin7
  N17: JP3.1, JP3.4, R1.Pin_1, JP4.1, JP4.4
  N18: R4.Pin_1, FET1.gate, R6.Pin_1
  N19: U4.1, U5.1, U6.1, Part2.+, C6.+
  N20: U4.2, U5.2, U6.2, Part2.-, C6.-

custom parts:
  Adafruit SHT31-D: Sensirion Temperature/Humidity sensors are some of the finest & highest-accuracy devices you can get. And, finally we have some that have a true I2C interface for easy reading. The SHT31-D sensor has an excellent ±2% relative humidity and ±0.3°C accuracy for most uses. We now use the version with a PTFE filter, it'll stay clean while still allowing humidity measurements to work Unlike earlier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
  Mini-360 DC-DC Buck converter: Mini-360 DC-DC Buck converter. Tiny buck step down voltage converter, input voltage 4.75 to 23V output 1 to 17V adjustable. Available from ebay and the like.
  LILYGO TTGO-T SIM7000G: LILYGO® TTGO T-SIM7000G Module ESP32-WROVER-B Chip WiFi Bluetooth 18560 Battery Holder Solar Charge Development Board.
  STP16NF06 N-Channel Power MOSFET: STP16NF06 N-channel Power MOSFET
